# Fritzing sketch buttons_and_led_matrix (saved by Fritzing 0.9.3b)
breadboards: 2

parts:
  Part1 = Adafruit Metro M0 Express
  S10 = Pushbutton [package="[THT]"]
  S9 = Pushbutton [package="[THT]"]
  S8 = Pushbutton [package="[THT]"]
  S7 = Pushbutton [package="[THT]"]
  S6 = Pushbutton [package="[THT]"]
  S4 = Pushbutton [package="[THT]"]
  S3 = Pushbutton [package="[THT]"]
  S5 = Pushbutton [package="[THT]"]
  S2 = Pushbutton [package="[THT]"]
  S1 = Pushbutton [package="[THT]"]
  R1 = Resistor [tolerance=±5% resistance=220 package=THT]
  shift_register_1 = 74HC595 SMD [package="SO16 [SMD]"]
  shift_register_2 = 74HC595 SMD [package="SO16 [SMD]"]
  LED3 = LED - 5mm [color="Red (633nm)" package="5 mm [THT]"]
  LED5 = LED - 5mm [color="Red (633nm)" package="5 mm [THT]"]
  LED4 = LED - 5mm [color="Red (633nm)" package="5 mm [THT]"]
  LED2 = LED - 5mm [color="Red (633nm)" package="5 mm [THT]"]
  LED1 = LED - 5mm [color="Red (633nm)" package="5 mm [THT]"]
  LED6 = LED - 5mm [color="Red (633nm)" package="5 mm [THT]"]
  LED7 = LED - 5mm [color="Red (633nm)" package="5 mm [THT]"]  # not connected
  LED8 = LED - 5mm [color="Red (633nm)" package="5 mm [THT]"]
  LED10 = LED - 5mm [color="Red (633nm)" package="5 mm [THT]"]
  LED9 = LED - 5mm [color="Red (633nm)" package="5 mm [THT]"]

nets (from the schematic view):
  N1: Part1.D13, S10.Pin_1, S10.Pin_2, S5.Pin_1, S5.Pin_2
  N2: Part1.D12, S9.Pin_1, S4.Pin_1, S4.Pin_2
  N3: Part1.D11, S3.Pin_1, S3.Pin_2
  N4: Part1.D10, S2.Pin_1, S2.Pin_2
  N5: Part1.D9, S6.Pin_1, S6.Pin_2, S1.Pin_1, S1.Pin_2
  N6: Part1.D7, S10.Pin_3, S10.Pin_4
  N7: Part1.D6, S4.Pin_3, S4.Pin_4, S3.Pin_3, S3.Pin_4, S5.Pin_3, S5.Pin_4, S2.Pin_3, S2.Pin_4, S1.Pin_3, S1.Pin_4
  N8: Part1.D5, shift_register_1.ST_CP, shift_register_2.ST_CP
  N9: Part1.D4, shift_register_1.SH_CP, shift_register_2.SH_CP
  N10: Part1.D3, shift_register_1.DS
  N11: S8.Pin_1, S8.Pin_2
  N12: S7.Pin_1, S7.Pin_2
  N13: R1.Pin_0, shift_register_1.GND
  N14: R1.Pin_1, shift_register_1.MR, shift_register_2.VCC
  N15: shift_register_1.Q1, LED2.anode
  N16: shift_register_1.Q2, LED3.anode
  N17: shift_register_1.Q3, LED4.anode
  N18: shift_register_1.Q4, LED5.anode
  N19: shift_register_1.Q5, LED6.anode
  N20: shift_register_1.Q7, LED8.anode
  N21: shift_register_1.Q7', shift_register_2.DS
  N22: shift_register_1.OE, shift_register_2.GND
  N23: shift_register_1.VCC, LED5.cathode
  N24: shift_register_2.Q1, LED10.anode
  N25: shift_register_2.Q0, LED9.anode
  N26: LED1.cathode, LED1.anode, LED6.cathode

custom parts:
  Adafruit Metro M0 Express: Metro is our series of microcontroller boards for use with the Arduino IDE. This new Metro board looks a whole lot like our original Metro 328, but with a huge upgrade. Instead of the ATmega328, this Metro features a ATSAMD21G18 chip, an ARM Cortex M0+. It's our first Metro that is designed for use with CircuitPython! CircuitPython is our beginner-oriented flavor of MicroPython - and as the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
